# Fritzing sketch schematic (saved by Fritzing 0.9.4)
breadboards: 1

parts:
  Part1 = Arduino Uno (Rev3)
  S1 = SWITCH-MOMENTARY-2 [package=tactile-pth-12mm]
  D1 = LTE-302 [package=lte-302]  # not connected
  LED1 = LED - 5mm [color="Red (633nm)" package="5 mm [THT]"]  # not connected
  R1 = Resistor [tolerance=±5% resistance=220 package="0603 [SMD]"]

nets:
  N1: Part1.D2, S1.2
  N2: Part1.5V, S1.1
  N3: Part1.GND, R1.Pin_0, R1.Pin_1
